# Fritzing sketch uext-molex-v2 (saved by Fritzing 0.9.4)
circuit board: 4.48386cm x 2.44175cm
perfboards: 1

parts:
  UEXT = shrouded pin header, 10 pins [form="♂ (shrouded male)"]
  I2C_3 = molex pin header, 4 pins [form=molex]
  I2C_1 = molex pin header, 4 pins [form=molex]
  I2C_2 = molex pin header, 4 pins [form=molex]
  I2C_0 = molex pin header, 4 pins [form=molex]

nets:
  N1: UEXT.pin1, I2C_3.pin1, I2C_1.pin1, I2C_2.pin1, I2C_0.pin1
  N2: UEXT.pin3, I2C_3.pin3, I2C_1.pin3, I2C_2.pin3, I2C_0.pin3
  N3: UEXT.pin8, I2C_3.pin4, I2C_1.pin4, I2C_2.pin4, I2C_0.pin4
  N4: UEXT.pin10, I2C_3.pin2, I2C_1.pin2, I2C_2.pin2, I2C_0.pin2

notes:
  uext-i2c
