# Fritzing sketch uext-molex (saved by Fritzing 0.9.4)
circuit board: 4.5cm x 2.5cm
perfboards: 1

parts:
  J1 = shrouded pin header, 10 pins [form="♂ (shrouded male)"]
  J5 = molex pin header, 4 pins [form=molex]
  J6 = molex pin header, 4 pins [form=molex]
  J7 = molex pin header, 4 pins [form=molex]
  J8 = molex pin header, 4 pins [form=molex]

nets:
  N1: J1.pin1, J5.pin1, J6.pin1, J7.pin1, J8.pin1
  N2: J1.pin3, J5.pin3, J6.pin3, J7.pin3, J8.pin3
  N3: J1.pin8, J5.pin4, J6.pin4, J7.pin4, J8.pin4
  N4: J1.pin10, J5.pin2, J6.pin2, J7.pin2, J8.pin2

notes:
  uext-i2c
